# Fritzing sketch smart-outlet (saved by Fritzing 0.9.3b)
circuit board: 8.46667cm x 5.64444cm
breadboards: 1

parts:
  D1 = Diode [package=diode-1n4148]
  R1 = Resistor [tolerance=±5% resistance=100k package=THT]
  C1 = Electrolytic Capacitor [capacitance=1µF package="100 mil [THT, electrolytic]"]
  IC1 = LM741 [part_number=LM741 package=dip08]
  J1 = female pin header, 3 pins [form="♀ (female)"]

nets:
  N1: D1.A, IC1.OUTPUT
  N2: D1.C, R1.Pin_1, C1.+, IC1.-INPUT
  GND: R1.Pin_0, C1.-, J1.pin1
  N3: IC1.+INPUT, J1.pin2
  -5V: IC1.V-
  5V: IC1.V+, J1.pin3

custom parts:
  LM741: General Purpose Operational Amplifier
